# Fritzing sketch sketch (saved by Fritzing 0.9.6b)

parts:
  U1 = ESP8266 NodeMCU LoLin module
  BAT1 = BC9VPC [package=bc9vpc]
  USBTTL1 = Micro USB B Plug
  KY-1 = Keyes Relay [package=THT]
  LED1 = LEDs [package=led10mm]

nets:
  N1: U1.D4, KY-1.signal
  N2: U1.Vin, KY-1.power
  N3: U1.GND, KY-1.ground
  N4: BAT1.V+, BAT1.V-, USBTTL1.usb
  N5: KY-1.C, LED1.C

custom parts:
  ESP8266 NodeMCU LoLin module: ESP8266 based NodeMCU
  Keyes Relay: The Keyes 5V relay module is suitable for SCM development, home appliance control. It uses a 5V~12V TIL control signal which can control DC / AC signal.
  LEDs: LEDs Standard schematic elements and footprints for 5mm, 3mm, 1206, and 0603 sized LEDs. 5mm - Spark Fun Electronics SKU : COM-00529 (and others)
